# Fritzing sketch duckveloper (saved by Fritzing 0.9.4)
breadboards: 1

parts:
  (Mounted_on_Arduino) = Arduino MP3 Player Shield
  Button = Pushbutton [package="[THT]"]
  part = Resistor [tolerance=±5% resistance=10k package=THT]
  LED1 = smd LED [color="Red (633nm)" package="0603 [SMD]"]
  R2 = Resistor [tolerance=±5% resistance=330 package=THT]
  SP1 = SPEAKER [package=pcb_mount_speaker]
  (Follow_the_Sparkfun_Mono_Audio_Amplifier_Quickstart_Guide) = TPA2000D1 Audio Amplifier [package="Breakout board Double Row DIL16"]

nets:
  N1: (Mounted_on_Arduino).GBUF, (Follow_the_Sparkfun_Mono_Audio_Amplifier_Quickstart_Guide).INN
  N2: (Mounted_on_Arduino).RIGHT, (Follow_the_Sparkfun_Mono_Audio_Amplifier_Quickstart_Guide).INP
  N3: (Mounted_on_Arduino).A5, LED1.anode
  N4: (Mounted_on_Arduino).D5, Button.Pin_3, Button.Pin_4
  N5: (Mounted_on_Arduino).D10, Button.Pin_1, Button.Pin_2, part.Pin_0
  N6: (Mounted_on_Arduino).5V-MOSI, (Follow_the_Sparkfun_Mono_Audio_Amplifier_Quickstart_Guide).PVDD
  N7: (Mounted_on_Arduino).GND, part.Pin_1, R2.Pin_1
  N8: LED1.cathode, R2.Pin_0
  N9: SP1.+, (Follow_the_Sparkfun_Mono_Audio_Amplifier_Quickstart_Guide).OUTP
  N10: SP1.-, (Follow_the_Sparkfun_Mono_Audio_Amplifier_Quickstart_Guide).OUTN
